# Fritzing sketch Design (saved by Fritzing 0.9.6b)
circuit board: 8.83926cm x 5.3226cm

parts:
  U1 = LCD-16X2 [package=lcd-16x2_nosilk]
  R2 = Trimmer Potentiometer [maximum_resistance=10kΩ package=THT]
  R3 = Resistor [tolerance=±5% resistance=220 package="2512 [SMD]"]
  Part2 = MicroSD Card Module
  DS1 = DS18B20 1-Wire Temperature Sensor [part_number=DS18B20]
  ZS-042_RTC1 = ZS-042 RTC Module
  R1 = Resistor [tolerance=±5% resistance=220 package="2512 [SMD]"]
  Arduino1 = Arduino Mini (Rev5)

nets:
  GND: U1.VSS, U1.R_W, U1.K, R2.leg2, Part2.GND, DS1.GND, ZS-042_RTC1.GND, Arduino1.GND
  VDD: U1.VDD, R2.leg1, R3.Pin_1, Part2.VCC, DS1.VDD, ZS-042_RTC1.VCC, R1.Pin_0, Arduino1.5V
  N1: U1.VO, R2.wiper
  N2: U1.RS, Arduino1.D9_PWM
  N3: U1.E, Arduino1.D8
  N4: U1.DB4, Arduino1.A0
  N5: U1.DB5, Arduino1.A1
  N6: U1.DB6, Arduino1.A2
  N7: U1.DB7, Arduino1.A3
  N8: U1.A, R3.Pin_0
  N9: Part2.MISO, Arduino1.D12
  N10: Part2.MOSI, Arduino1.D11_PWM
  N11: Part2.SCK, Arduino1.D13
  N12: Part2.CS, Arduino1.D7
  N13: DS1.DQ, R1.Pin_1, Arduino1.D6_PWM
  N14: ZS-042_RTC1.SDA, Arduino1.A4
  N15: ZS-042_RTC1.SCL, Arduino1.A5
  N16: ZS-042_RTC1.SQW, Arduino1.D2
